# Fritzing sketch bosung (saved by Fritzing 0.9.3b)
breadboards: 1

parts:
  M1 = DC Motor
  KY-1 = Keyes Relay [package=THT]
  VCC1 = Battery

nets:
  N1: M1.pin_1, KY-1.C
  N2: M1.pin_2, VCC1.+
  N3: KY-1.NO, VCC1.-

notes:
  8vDC
  Relay
  Bơm nước

custom parts:
  Keyes Relay: The Keyes 5V relay module is suitable for SCM development, home appliance control. It uses a 5V~12V TIL control signal which can control DC / AC signal.
